# Fritzing sketch PIRPiezoSpeakerUno9V (saved by Fritzing 0.9.2b)

parts:
  Piezo_Speaker = Piezo Speaker
  BC337 = TRANSISTOR_NPN_2 [package=to-92]
  part = Resistor [tolerance=±5% resistance=1k package="1206 [SMD]"]
  D2 = Rectifier Diode [part_number=Rectifier package="Melf DO-213 AA [SMD]"]
  Part1 = Arduino Uno (Rev3) - ICSP
  part_2 = Battery block 9V
  PIR1 = PIR sensor
  part_3 = Resistor [tolerance=±5% resistance=10k package="0805 [SMD]"]

nets:
  N1: Piezo_Speaker.pin1, BC337.C, D2.anode
  5V: Piezo_Speaker.pin2, D2.cathode, Part1.5V, PIR1.VCC, part_3.Pin_0
  N2: BC337.B, part.Pin_0
  GND: BC337.E, Part1.GND, part_2.-, PIR1.GND
  N3: part.Pin_1, Part1.D3_PWM
  N4: Part1.D10_PWM/SS, PIR1.SIG, part_3.Pin_1
  N5: Part1.VIN, part_2.+
